# Fritzing sketch ArduinoKeyboard (saved by Fritzing 0.9.5d)
breadboards: 1

parts:
  Part1 = Arduino Leonardo (Rev3b)
  U1 = mystery part, 5 pins [chip_label="Guitar Hero Grip"]
  R1 = Resistor [tolerance=±5% resistance=10000 package=THT]
  R2 = Resistor [tolerance=±5% resistance=10000 package=THT]
  R3 = Resistor [tolerance=±5% resistance=10000 package=THT]
  R4 = Resistor [tolerance=±5% resistance=10000 package=THT]

nets:
  N1: Part1.3V3, R1.Pin_0, R2.Pin_0, R3.Pin_0, R4.Pin_0
  N2: Part1.GND, U1.pin5
  N3: Part1.D8/A8, U1.pin1, R4.Pin_1
  N4: Part1.D9_PWM/A9, U1.pin2, R3.Pin_1
  N5: Part1.D10_PWM/A10, U1.pin3, R2.Pin_1
  N6: Part1.D11_PWM, U1.pin4, R1.Pin_1
